# Fritzing sketch Project2_schematic (saved by Fritzing 0.9.4)
breadboards: 1

parts:
  Part1 = Adafruit HUZZAH32 ESP32 Feather [part_number="Adafruit #3405"]
  R2 = Resistor [tolerance=±5% resistance=430 package=THT]
  R3 = Resistor [tolerance=±5% resistance=430 package=THT]
  R5 = Resistor [tolerance=±5% resistance=1k package=THT]
  LED1 = RGB LED (com. cathode, rgb) [package="5 mm [THT]"]
  R7 = Resistor [tolerance=±5% resistance=470 package=THT]
  S1 = Pushbutton [package="[THT]"]
  U1 = POT [package=3362u]

nets:
  N1: Part1.A1_DAC1, R5.Pin_1, S1.Pin_3, S1.Pin_4
  N2: Part1.A0_DAC2, U1.S
  N3: Part1.GND, R5.Pin_0, LED1.common_cathode, U1.E
  N4: Part1.3.3V, S1.Pin_1, S1.Pin_2, U1.A
  N5: Part1.IO12_A11, R7.Pin_0
  N6: Part1.IO27_A10, R2.Pin_0
  N7: Part1.IO33_A9, R3.Pin_0
  N8: R2.Pin_1, LED1.green_anode
  N9: R3.Pin_1, LED1.blue_anode
  N10: LED1.red_anode, R7.Pin_1
